# Fritzing sketch Untitled Sketch 2 (saved by Fritzing 0.9.3b)
breadboards: 1

parts:
  Componente1 = Arduino Uno (Rev3)
  PIR1 = PIR sensor
  DHT1 = DHT11 Humitidy and Temperature Sensor
  R1 = Photocell (LDR) [package=THT]  # not connected
  R2 = Resistor [tolerance=±5% resistance=220 package="0805 [SMD]"]

nets:
  N1: Componente1.A0, PIR1.SIG
  N2: Componente1.A1, R2.Pin_0
  N3: Componente1.A2, DHT1.DATA
  VDD: Componente1.5V, PIR1.VDD, DHT1.VDD
  GND: Componente1.GND, PIR1.GND, DHT1.GND, R2.Pin_1

custom parts:
  DHT11 Humitidy and Temperature Sensor: DHT11 Humidity and Temperature Sensor
