# Fritzing sketch tsl (saved by Fritzing 0.9.3b)
breadboards: 1

parts:
  Componente1 = Arduino Uno (Rev3) - ICSP
  LED1 = LED - 3mm [color="Blue (470nm)" package="3 mm [THT]"]
  Componente2 = Adafruit TSL2561 [part_number="Adafruit #439"]
  R1 = Resistor [tolerance=±1% resistance=110 package=THT]

nets:
  N1: Componente1.A4/SDA, Componente2.SDA
  N2: Componente1.A5/SCL, Componente2.SCL
  N3: Componente1.D13/SCK, R1.Pin_1
  GND: Componente1.GND, LED1.cathode, Componente2.GND
  3V3: Componente1.3V3, Componente2.3.3V
  N4: LED1.anode, R1.Pin_0

custom parts:
  Adafruit TSL2561: The TSL2561 luminosity sensor is an advanced digital light sensor, ideal for use in a wide range of light situations. Compared to low cost CdS cells, this sensor is more precise, allowing for exact lux calculations and can be configured for different gain/timing ranges to detect light ranges from up to 0.1 - 40,000+ Lux on the fly. The best part of this sensor is that it contains both infrared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
